// Logisim project alu.circ as structural Verilog: 1 circuit, main circuit alu
module alu (
  input  [31:0] A,
  input  [31:0] B,
  input  [3:0] ALUSel,
  output [31:0] ALUResult
);

  wire comparator_1_lt;
  wire [31:0] add0, AND_out, mul, mulh, mulhu, OR_Out, SLLS, slt, SRAS, srll, sub, XOR_OUTPUT;

  assign XOR_OUTPUT = A ^ B;  // XOR_Gate xor_1, 32 bits wide
  Shifter #(.shift("lr"), .width(32)) shifter_1 (.in(A), .\dist (B[4:0]), .out(srll));
  Shifter #(.width(32)) shifter_2 (.in(A), .\dist (B[4:0]), .out(SLLS));
  Adder #(.width(32)) adder_1 (.a(A), .b(B), .out(add0), .cin(1'b0));  // open: cout
  assign OR_Out = A | B;  // OR_Gate or_1, 32 bits wide
  assign AND_out = A & B;  // AND_Gate and_1, 32 bits wide
  Multiplier #(.mode("twosComplement"), .width(32)) multiplier_1 (.a(A), .b(B), .out(mul), .cout(mulh));  // open: cin
  Multiplier #(.width(32)) multiplier_2 (.a(A), .b(B), .cout(mulhu));  // open: out, cin
  Shifter #(.shift("ar"), .width(32)) shifter_3 (.in(A), .\dist (B[4:0]), .out(SRAS));
  Multiplexer #(.select(4), .width(32)) multiplexer_1 (
    .in0(add0), .in1(SLLS), .in2(slt), .in3({32{1'b0}}), .in4(XOR_OUTPUT), .in5(srll), .in6(OR_Out),
    .in7(AND_out), .in8(mul), .in9(mulh), .in10({32{1'b0}}), .in11(mulhu), .in12(sub), .in13(SRAS),
    .in14({32{1'b0}}), .in15(B), .out(ALUResult), .sel(ALUSel));
  Subtractor #(.width(32)) subtractor_1 (.a(A), .b(B), .out(sub), .bin(1'b0));  // open: bout
  Comparator #(.width(32)) comparator_1 (.a(A), .b(B), .lt(comparator_1_lt));  // open: gt, eq
  assign slt = {{31{1'b0}}, comparator_1_lt};  // Bit_Extender bit_extender_1

  // Notes on the sheet:
  //   INPUTS to your circuit
  //   DON'T CHANGE THE LOCATIONS OF THE INPUTS AND OUTPUTS!
  //   OUTPUT from your circuit
endmodule
