// Logisim project control-logic.circ as structural Verilog: 1 circuit, main circuit control_logic
module control_logic (
  input  [31:0] Instruction,
  input  BrEq,
  input  BrLt,
  output PCSel,
  output RegWEn,
  output [2:0] ImmSel,
  output BrUn,
  output ASel,
  output BSel,
  output [3:0] ALUSel,
  output MemWEn,
  output [1:0] WBSel
);

  wire add, addi, and_1, and_1_out, and_2_out, and_3_out, and_4_out, and_5_out, and_6_out, and_7_out,
       and_20_out, and_21_out, and_22_out, and_35_out, and_39_out, and_40_out, and_41_out, and_48_out,
       and_49_out, andi, auipc, b_type, beq, bge, bgeu, blt, bltu, bne, comparator_1_eq, comparator_2_eq,
       comparator_3_eq, comparator_4_eq, comparator_5_eq, comparator_6_eq, comparator_11_eq,
       comparator_12_eq, comparator_13_eq, comparator_14_eq, comparator_15_eq, comparator_16_eq,
       comparator_17_eq, comparator_18_eq, comparator_19_eq, comparator_20_eq, comparator_21_eq,
       comparator_22_eq, comparator_23_eq, comparator_24_eq, comparator_25_eq, comparator_26_eq,
       comparator_27_eq, comparator_28_eq, comparator_29_eq, comparator_30_eq, comparator_31_eq,
       comparator_32_eq, comparator_33_eq, comparator_34_eq, comparator_35_eq, comparator_36_eq,
       comparator_37_eq, comparator_38_eq, comparator_39_eq, comparator_41_eq, comparator_42_eq,
       comparator_45_eq, comparator_46_eq, comparator_47_eq, comparator_48_eq, comparator_49_eq,
       comparator_50_eq, comparator_51_eq, comparator_52_eq, comparator_53_eq, i_type, jal, jalr, l_type, lb,
       lh, lui, lw, mul, mulh, mulhu, not_1_out, not_2_out, not_3_out, or_1, or_2_out, or_3_out, or_4_out,
       or_5_out, ori, priority_encoder_1_gs, r_type, s_type, sb, sh, sll_1, slli, slt, slti, sra_1, srai,
       srl_1, srli, sub, sw, xor_1, xori;
  wire [1:0] priority_encoder_1_out;
  wire [4:0] priority_encoder_2_out;
  wire [5:0] adder_1_out, bit_extender_1_out, bit_extender_2_out, rom_input;
  wire [15:14] rom_1_data;

  Comparator #(.width(3)) comparator_1 (.a(Instruction[14:12]), .b(3'b000), .eq(comparator_1_eq));  // open: gt, lt
  Comparator #(.width(3)) comparator_2 (.a(Instruction[14:12]), .b(3'b000), .eq(comparator_2_eq));  // open: gt, lt
  Comparator #(.width(3)) comparator_3 (.a(Instruction[14:12]), .b(3'b001), .eq(comparator_3_eq));  // open: gt, lt
  Comparator #(.width(3)) comparator_4 (.a(Instruction[14:12]), .b(3'b001), .eq(comparator_4_eq));  // open: gt, lt
  Comparator #(.width(7)) comparator_5 (.a(Instruction[6:0]), .b(7'b0010011), .eq(comparator_5_eq));  // open: gt, lt
  Comparator #(.width(7)) comparator_6 (.a(Instruction[6:0]), .b(7'b1100111), .eq(comparator_6_eq));  // open: gt, lt
  Comparator #(.width(7)) comparator_7 (.a(Instruction[6:0]), .b(7'b0110011), .eq(r_type));  // open: gt, lt
  Comparator #(.width(7)) comparator_8 (.a(Instruction[6:0]), .b(7'b1100011), .eq(b_type));  // open: gt, lt
  Comparator #(.width(7)) comparator_9 (.a(Instruction[6:0]), .b(7'b0000011), .eq(l_type));  // open: gt, lt
  Comparator #(.width(7)) comparator_10 (.a(Instruction[6:0]), .b(7'b0100011), .eq(s_type));  // open: gt, lt
  Comparator #(.width(3)) comparator_11 (.a(Instruction[14:12]), .b(3'b000), .eq(comparator_11_eq));  // open: gt, lt
  Comparator #(.width(3)) comparator_12 (.a(Instruction[14:12]), .b(3'b101), .eq(comparator_12_eq));  // open: gt, lt
  Comparator #(.width(3)) comparator_13 (.a(Instruction[14:12]), .b(3'b101), .eq(comparator_13_eq));  // open: gt, lt
  ROM #(.addrWidth(6), .dataWidth(16)) rom_1 (
    .addr(rom_input), .data({rom_1_data, WBSel, MemWEn, ALUSel, BSel, ASel, BrUn, ImmSel, RegWEn}));
  or u_or_1 (i_type, comparator_5_eq, comparator_6_eq);
  and u_and_1 (and_1_out, r_type, comparator_1_eq);
  Comparator #(.width(7)) comparator_14 (.a(Instruction[31:25]), .b({7{1'b0}}), .eq(comparator_14_eq));  // open: gt, lt
  and and_2 (and_2_out, r_type, comparator_2_eq);
  Comparator #(.width(7)) comparator_15 (
    .a(Instruction[31:25]), .b(7'b0100000), .eq(comparator_15_eq));  // open: gt, lt
  and and_3 (and_3_out, r_type, comparator_11_eq);
  Comparator #(.width(7)) comparator_16 (
    .a(Instruction[31:25]), .b(7'b0000001), .eq(comparator_16_eq));  // open: gt, lt
  and and_4 (and_4_out, r_type, comparator_12_eq);
  Comparator #(.width(7)) comparator_17 (.a(Instruction[31:25]), .b({7{1'b0}}), .eq(comparator_17_eq));  // open: gt, lt
  and and_5 (and_5_out, r_type, comparator_13_eq);
  Comparator #(.width(7)) comparator_18 (
    .a(Instruction[31:25]), .b(7'b0100000), .eq(comparator_18_eq));  // open: gt, lt
  and and_6 (and_6_out, r_type, comparator_3_eq);
  Comparator #(.width(7)) comparator_19 (.a(Instruction[31:25]), .b({7{1'b0}}), .eq(comparator_19_eq));  // open: gt, lt
  and and_7 (and_7_out, r_type, comparator_4_eq);
  Comparator #(.width(7)) comparator_20 (
    .a(Instruction[31:25]), .b(7'b0000001), .eq(comparator_20_eq));  // open: gt, lt
  and and_8 (add, and_1_out, comparator_14_eq);
  and and_9 (sub, and_2_out, comparator_15_eq);
  and and_10 (mul, and_3_out, comparator_16_eq);
  and and_11 (srl_1, and_4_out, comparator_17_eq);
  and and_12 (sra_1, and_5_out, comparator_18_eq);
  and and_13 (sll_1, and_6_out, comparator_19_eq);
  and and_14 (mulh, and_7_out, comparator_20_eq);
  Comparator #(.width(3)) comparator_21 (.a(Instruction[14:12]), .b(3'b000), .eq(comparator_21_eq));  // open: gt, lt
  Comparator #(.width(3)) comparator_22 (.a(Instruction[14:12]), .b(3'b111), .eq(comparator_22_eq));  // open: gt, lt
  Comparator #(.width(3)) comparator_23 (.a(Instruction[14:12]), .b(3'b110), .eq(comparator_23_eq));  // open: gt, lt
  Comparator #(.width(3)) comparator_24 (.a(Instruction[14:12]), .b(3'b100), .eq(comparator_24_eq));  // open: gt, lt
  Comparator #(.width(3)) comparator_25 (.a(Instruction[14:12]), .b(3'b010), .eq(comparator_25_eq));  // open: gt, lt
  Comparator #(.width(3)) comparator_26 (.a(Instruction[14:12]), .b(3'b001), .eq(comparator_26_eq));  // open: gt, lt
  Comparator #(.width(3)) comparator_27 (.a(Instruction[14:12]), .b(3'b101), .eq(comparator_27_eq));  // open: gt, lt
  Comparator #(.width(3)) comparator_28 (.a(Instruction[14:12]), .b(3'b101), .eq(comparator_28_eq));  // open: gt, lt
  and and_15 (addi, i_type, comparator_21_eq);
  and and_16 (andi, i_type, comparator_22_eq);
  and and_17 (ori, i_type, comparator_23_eq);
  and and_18 (xori, i_type, comparator_24_eq);
  and and_19 (slti, i_type, comparator_25_eq);
  and and_20 (and_20_out, i_type, comparator_26_eq);
  and and_21 (and_21_out, i_type, comparator_27_eq);
  and and_22 (and_22_out, i_type, comparator_28_eq);
  Comparator #(.width(3)) comparator_29 (.a(Instruction[14:12]), .b(3'b111), .eq(comparator_29_eq));  // open: gt, lt
  Comparator #(.width(3)) comparator_30 (.a(Instruction[14:12]), .b(3'b110), .eq(comparator_30_eq));  // open: gt, lt
  Comparator #(.width(3)) comparator_31 (.a(Instruction[14:12]), .b(3'b100), .eq(comparator_31_eq));  // open: gt, lt
  Comparator #(.width(3)) comparator_32 (.a(Instruction[14:12]), .b(3'b010), .eq(comparator_32_eq));  // open: gt, lt
  Comparator #(.width(3)) comparator_33 (.a(Instruction[14:12]), .b(3'b011), .eq(comparator_33_eq));  // open: gt, lt
  Comparator #(.width(3)) comparator_34 (.a(Instruction[14:12]), .b(3'b000), .eq(comparator_34_eq));  // open: gt, lt
  Comparator #(.width(3)) comparator_35 (.a(Instruction[14:12]), .b(3'b001), .eq(comparator_35_eq));  // open: gt, lt
  Comparator #(.width(3)) comparator_36 (.a(Instruction[14:12]), .b(3'b010), .eq(comparator_36_eq));  // open: gt, lt
  Comparator #(.width(3)) comparator_37 (.a(Instruction[14:12]), .b(3'b000), .eq(comparator_37_eq));  // open: gt, lt
  Comparator #(.width(3)) comparator_38 (.a(Instruction[14:12]), .b(3'b001), .eq(comparator_38_eq));  // open: gt, lt
  Comparator #(.width(3)) comparator_39 (.a(Instruction[14:12]), .b(3'b010), .eq(comparator_39_eq));  // open: gt, lt
  Comparator #(.width(7)) comparator_40 (.a(Instruction[6:0]), .b(7'b1101111), .eq(jal));  // open: gt, lt
  Comparator #(.width(7)) comparator_41 (.a(Instruction[6:0]), .b(7'b1100111), .eq(comparator_41_eq));  // open: gt, lt
  Comparator #(.width(3)) comparator_42 (.a(Instruction[14:12]), .b(3'b000), .eq(comparator_42_eq));  // open: gt, lt
  Comparator #(.width(7)) comparator_43 (.a(Instruction[6:0]), .b(7'b0010111), .eq(auipc));  // open: gt, lt
  Comparator #(.width(7)) comparator_44 (.a(Instruction[6:0]), .b(7'b0110111), .eq(lui));  // open: gt, lt
  Comparator #(.width(7)) comparator_45 (.a(Instruction[31:25]), .b({7{1'b0}}), .eq(comparator_45_eq));  // open: gt, lt
  Comparator #(.width(7)) comparator_46 (.a(Instruction[31:25]), .b({7{1'b0}}), .eq(comparator_46_eq));  // open: gt, lt
  Comparator #(.width(7)) comparator_47 (
    .a(Instruction[31:25]), .b(7'b0100000), .eq(comparator_47_eq));  // open: gt, lt
  and and_23 (and_1, r_type, comparator_29_eq);
  and and_24 (or_1, r_type, comparator_30_eq);
  and and_25 (xor_1, r_type, comparator_31_eq);
  and and_26 (slt, r_type, comparator_32_eq);
  and and_27 (mulhu, r_type, comparator_33_eq);
  and and_28 (lb, l_type, comparator_34_eq);
  and and_29 (lh, l_type, comparator_35_eq);
  and and_30 (lw, l_type, comparator_36_eq);
  and and_31 (sb, s_type, comparator_37_eq);
  and and_32 (sh, s_type, comparator_38_eq);
  and and_33 (sw, s_type, comparator_39_eq);
  and and_34 (jalr, comparator_41_eq, comparator_42_eq);
  and and_35 (and_35_out, beq, BrEq);
  not not_1 (not_1_out, BrEq);
  and and_36 (slli, and_20_out, comparator_45_eq);
  and and_37 (srli, and_21_out, comparator_46_eq);
  and and_38 (srai, and_22_out, comparator_47_eq);
  and and_39 (and_39_out, bne, not_1_out);
  or or_2 (or_2_out, and_35_out, and_39_out);
  and and_40 (and_40_out, blt, BrLt);
  or or_3 (or_3_out, or_2_out, and_40_out);
  and and_41 (and_41_out, bltu, BrLt);
  Comparator #(.width(3)) comparator_48 (.a(Instruction[14:12]), .b(3'b000), .eq(comparator_48_eq));  // open: gt, lt
  Comparator #(.width(3)) comparator_49 (.a(Instruction[14:12]), .b(3'b101), .eq(comparator_49_eq));  // open: gt, lt
  Comparator #(.width(3)) comparator_50 (.a(Instruction[14:12]), .b(3'b111), .eq(comparator_50_eq));  // open: gt, lt
  Comparator #(.width(3)) comparator_51 (.a(Instruction[14:12]), .b(3'b110), .eq(comparator_51_eq));  // open: gt, lt
  Comparator #(.width(3)) comparator_52 (.a(Instruction[14:12]), .b(3'b001), .eq(comparator_52_eq));  // open: gt, lt
  or or_4 (or_4_out, or_3_out, and_41_out);
  Comparator #(.width(3)) comparator_53 (.a(Instruction[14:12]), .b(3'b100), .eq(comparator_53_eq));  // open: gt, lt
  not not_2 (not_2_out, BrLt);
  and and_42 (beq, b_type, comparator_48_eq);
  and and_43 (bge, b_type, comparator_49_eq);
  and and_44 (bgeu, b_type, comparator_50_eq);
  and and_45 (blt, b_type, comparator_53_eq);
  and and_46 (bltu, b_type, comparator_51_eq);
  and and_47 (bne, b_type, comparator_52_eq);
  and and_48 (and_48_out, bge, not_2_out);
  or or_5 (or_5_out, or_4_out, and_48_out);
  not not_3 (not_3_out, BrLt);
  and and_49 (and_49_out, bgeu, not_3_out);
  or or_6 (PCSel, jal, jalr, or_5_out, and_49_out);
  Priority_Encoder #(.select(2)) priority_encoder_1 (
    .in0(auipc), .in1(lui), .in2(jal), .in3(jalr), .out(priority_encoder_1_out), .gs(priority_encoder_1_gs));  // open: en_out, en_in
  Priority_Encoder #(.select(5)) priority_encoder_2 (
    .in0(add), .in1(mul), .in2(sub), .in3(sll_1), .in4(mulh), .in5(mulhu), .in6(slt), .in7(xor_1),
    .in8(srl_1), .in9(sra_1), .in10(or_1), .in11(and_1), .in12(lb), .in13(lh), .in14(lw), .in15(addi),
    .in16(slli), .in17(slti), .in18(xori), .in19(srli), .in20(srai), .in21(ori), .in22(andi), .in23(sb),
    .in24(sh), .in25(sw), .in26(beq), .in27(bne), .in28(blt), .in29(bge), .in30(bltu), .in31(bgeu),
    .out(priority_encoder_2_out));  // open: gs, en_out, en_in
  assign bit_extender_1_out = {{4{1'b0}}, priority_encoder_1_out};  // Bit_Extender bit_extender_1
  assign bit_extender_2_out = {{1{1'b0}}, priority_encoder_2_out};  // Bit_Extender bit_extender_2
  Adder #(.width(6)) adder_1 (.a(bit_extender_1_out), .b(6'b100000), .out(adder_1_out));  // open: cin, cout
  Multiplexer #(.enable("false"), .width(6)) multiplexer_1 (
    .in0(bit_extender_2_out), .in1(adder_1_out), .out(rom_input), .sel(priority_encoder_1_gs));

  // Other names for the same wires on the sheet: opcode[6:0] = Instruction[6:0]; funct3[2:0] = Instruction[14:12];
  //   funct7[6:0] = Instruction[31:25]

  // Notes on the sheet:
  //   INPUTS to your circuit
  //   Connect ROM Input here ->
  //   contents of rom_1 (hex, n*v repeats v):
  //   1001 1401 1601 1081 1481 1581 1101 1201 1281 1681 1301 1381 2041 2041 2041 1041 10c1 1141 1241 12c1
  //   16c1 1341 13c1 842 842 842 4*1064 1074 1074 1067 17c7 69 41
  //   ROM FOR CONTROL LOGIC
  //   DON'T CHANGE THE LOCATIONS OF THE INPUTS AND OUTPUTS!
  //   This is only if you choose to do the ROM option
  //   OUTPUT from your circuit
  //   Reminder: If using ROM, use combinational logic for PCSel
endmodule
