// Logisim project cpu.circ as structural Verilog: 1 circuit, main circuit cpu
module cpu (
  input  clk,
  input  [31:0] Instruction,
  input  [31:0] MemReadData,
  output [31:0] MemAddress,
  output [31:0] ProgramCounter,
  output [31:0] ra,
  output [31:0] sp,
  output [31:0] t0,
  output [31:0] t1,
  output [31:0] t2,
  output [31:0] s0,
  output [31:0] s1,
  output [31:0] a0,
  output [3:0] MemWriteMask,
  output [31:0] MemWriteData
);

  wire branch_comp_1_breq, branch_comp_1_brlt, control_logic_1_asel, control_logic_1_brun,
       control_logic_1_bsel, control_logic_1_memwen, control_logic_1_regwen, PCSel, undriven, undriven_2;
  wire [1:0] control_logic_1_wbsel;
  wire [2:0] control_logic_1_immsel;
  wire [3:0] control_logic_1_alusel;
  wire [31:0] adder_1_out, adder_2_out, imm_gen_1_immediate, inst, load_data, multiplexer_1_out,
       multiplexer_2_out, multiplexer_3_out, multiplexer_4_out, pc, RS1, RS2, WB_RES;

  Adder #(.width(32)) adder_1 (.a(ProgramCounter), .b(32'h4), .out(adder_1_out));  // open: cin, cout
  Register #(.width(32)) register_1 (.D(multiplexer_1_out), .en(undriven), .clk(clk), .Q(inst));  // open: clr
  Multiplexer #(.width(32)) multiplexer_1 (.in0(Instruction), .in1(32'h13), .out(multiplexer_1_out), .sel(PCSel));
  Multiplexer #(.width(32)) multiplexer_2 (.in0(adder_1_out), .in1(MemAddress), .out(multiplexer_2_out), .sel(PCSel));
  Register #(.width(32)) u_PC (.D(multiplexer_2_out), .en(undriven_2), .clk(clk), .Q(ProgramCounter));  // open: clr
  Register #(.width(32)) register_2 (.D(ProgramCounter), .clk(clk), .Q(pc));  // open: en, clr
  control_logic control_logic_1 (
    .Instruction(inst), .BrEq(branch_comp_1_breq), .BrLt(branch_comp_1_brlt), .PCSel(PCSel),
    .RegWEn(control_logic_1_regwen), .ImmSel(control_logic_1_immsel), .BrUn(control_logic_1_brun),
    .ASel(control_logic_1_asel), .BSel(control_logic_1_bsel), .ALUSel(control_logic_1_alusel),
    .MemWEn(control_logic_1_memwen), .WBSel(control_logic_1_wbsel));
  regfile regfile_1 (
    .ReadIndex1(inst[19:15]), .ReadIndex2(inst[24:20]), .WriteIndex(inst[11:7]), .WriteData(WB_RES),
    .RegWEn(control_logic_1_regwen), .clk(clk), .ra(ra), .sp(sp), .t0(t0), .t1(t1), .t2(t2), .s0(s0),
    .s1(s1), .a0(a0), .ReadData1(RS1), .ReadData2(RS2));
  imm_gen imm_gen_1 (.Instruction(inst), .ImmSel(control_logic_1_immsel), .Immediate(imm_gen_1_immediate));
  branch_comp branch_comp_1 (
    .BrData1(RS1), .BrData2(RS2), .BrUn(control_logic_1_brun), .BrEq(branch_comp_1_breq),
    .BrLt(branch_comp_1_brlt));
  Multiplexer #(.width(32)) multiplexer_3 (.in0(RS1), .in1(pc), .out(multiplexer_3_out), .sel(control_logic_1_asel));
  Multiplexer #(.width(32)) multiplexer_4 (
    .in0(RS2), .in1(imm_gen_1_immediate), .out(multiplexer_4_out), .sel(control_logic_1_bsel));
  alu alu_1 (.A(multiplexer_3_out), .B(multiplexer_4_out), .ALUSel(control_logic_1_alusel), .ALUResult(MemAddress));
  partial_store partial_store_1 (
    .Instruction(inst), .MemAddress(MemAddress), .DataFromReg(RS2), .MemWEn(control_logic_1_memwen),
    .MemWriteMask(MemWriteMask), .DataToMem(MemWriteData));
  Adder #(.width(32)) adder_2 (.a(pc), .b(32'h4), .out(adder_2_out));  // open: cin, cout
  partial_load partial_load_1 (
    .Instruction(inst), .MemAddress(MemAddress), .DataFromMem(MemReadData), .DataToReg(load_data));
  Multiplexer #(.select(2), .width(32)) multiplexer_5 (
    .in0(load_data), .in1(MemAddress), .in2(adder_2_out), .out(WB_RES), .sel(control_logic_1_wbsel));  // open: in3

  // Other names for the same wires on the sheet: ALURes[31:0] = MemAddress

  // Notes on the sheet:
  //   To IMEM
  //   IMEM (do **NOT** move this)
  //   From IMEM
  //   Inputs/Outputs for testing. Do **NOT** move these.
  //   It is OK to move the PC, RegFile, ALU, MEM, Branch Comp, Imm Gen, Partial Load, Partial Store and Control Logic to wherever is most convenient for you when constructing your CPU, and to delete this text
  //   To DMEM
  //   DMEM (do **NOT** move this)
  //   From DMEM
endmodule
