// Logisim project imm-gen.circ as structural Verilog: 1 circuit, main circuit imm_gen
module imm_gen (
  input  [31:0] Instruction,
  input  [2:0] ImmSel,
  output [31:0] Immediate
);

  wire and_1_out, comparator_1_eq, comparator_2_eq, comparator_3_eq, comparator_4_eq, not_1_out, or_1_out;
  wire [11:0] bit_extender_3_out;
  wire [12:0] bit_extender_2_out, shifter_2_out;
  wire [31:0] adder_1_out, bit_extender_1_out, bit_extender_4_out, bit_extender_5_out, bit_extender_6_out,
       demultiplexer_1_out0, demultiplexer_1_out1, shifter_1_out, shifter_3_out;

  Comparator #(.width(3)) comparator_1 (.a(Instruction[14:12]), .b(3'b001), .eq(comparator_1_eq));  // open: gt, lt
  Comparator #(.width(3)) comparator_2 (.a(Instruction[14:12]), .b(3'b101), .eq(comparator_2_eq));  // open: gt, lt
  or or_1 (or_1_out, comparator_1_eq, comparator_2_eq);
  Comparator #(.width(7)) comparator_3 (.a(Instruction[6:0]), .b(7'b0000011), .eq(comparator_3_eq));  // open: gt, lt
  assign bit_extender_1_out = {{20{Instruction[31]}}, {Instruction[31:25], Instruction[11:7]}};  // Bit_Extender bit_extender_1
  assign bit_extender_2_out = {{1{1'b0}}, {Instruction[31], Instruction[7], Instruction[30:25], Instruction[11:8]}};  // Bit_Extender bit_extender_2
  Shifter #(.shift("lr"), .width(32)) shifter_1 (.in(Instruction), .\dist (5'b01100), .out(shifter_1_out));
  assign bit_extender_3_out = {{11{Instruction[31]}}, Instruction[31]};  // Bit_Extender bit_extender_3
  Comparator #(.width(1)) comparator_4 (.a(or_1_out), .b(1'b1), .eq(comparator_4_eq));  // open: gt, lt
  not not_1 (not_1_out, comparator_3_eq);
  Shifter #(.width(13)) shifter_2 (.in(bit_extender_2_out), .\dist (4'b0001), .out(shifter_2_out));
  Shifter #(.width(32)) shifter_3 (.in(shifter_1_out), .\dist (5'b01100), .out(shifter_3_out));
  and and_1 (and_1_out, comparator_4_eq, not_1_out);
  assign bit_extender_4_out = {{19{shifter_2_out[12]}}, shifter_2_out};  // Bit_Extender bit_extender_4
  Demultiplexer #(.width(32)) demultiplexer_1 (
    .out0(demultiplexer_1_out0), .out1(demultiplexer_1_out1), .in(Instruction), .sel(and_1_out));
  assign bit_extender_5_out = {{20{demultiplexer_1_out0[31]}}, demultiplexer_1_out0[31:20]};  // Bit_Extender bit_extender_5
  assign bit_extender_6_out = {{27{1'b0}}, demultiplexer_1_out1[24:20]};  // Bit_Extender bit_extender_6
  Adder #(.width(32)) adder_1 (.a(bit_extender_5_out), .b(bit_extender_6_out), .out(adder_1_out));  // open: cin, cout
  Multiplexer #(.select(3), .width(32)) multiplexer_1 (
    .in0(adder_1_out), .in1(bit_extender_1_out), .in2(bit_extender_4_out), .in3(shifter_3_out),
    .in4({bit_extender_3_out, Instruction[19:12], Instruction[20], Instruction[30:21], 1'b0}),
    .out(Immediate), .sel(ImmSel));  // open: in5, in6, in7

  // Other names for the same wires on the sheet: Funct3[2:0] = Instruction[14:12]; Opcode[6:0] = Instruction[6:0]

  // Notes on the sheet:
  //   INPUTS to your circuit
  //   DON'T CHANGE THE LOCATIONS OF THE INPUTS AND OUTPUTS!
  //   OUTPUT from your circuit
endmodule
