// Logisim project partial-load.circ as structural Verilog: 1 circuit, main circuit partial_load
module partial_load (
  input  [31:0] Instruction,
  input  [31:0] MemAddress,
  input  [31:0] DataFromMem,
  output [31:0] DataToReg
);

  wire [1:0] BOT_TWO_BITS;
  wire [31:0] bit_extender_1_out, bit_extender_2_out, bit_extender_3_out, bit_extender_4_out,
       bit_extender_5_out, bit_extender_6_out, bit_extender_7_out, multiplexer_1_out, multiplexer_2_out;

  assign bit_extender_1_out = {{24{DataFromMem[7]}}, DataFromMem[7:0]};  // Bit_Extender bit_extender_1
  assign bit_extender_2_out = {{24{DataFromMem[15]}}, DataFromMem[15:8]};  // Bit_Extender bit_extender_2
  assign bit_extender_3_out = {{24{DataFromMem[23]}}, DataFromMem[23:16]};  // Bit_Extender bit_extender_3
  assign bit_extender_4_out = {{24{DataFromMem[31]}}, DataFromMem[31:24]};  // Bit_Extender bit_extender_4
  assign bit_extender_5_out = {{16{DataFromMem[15]}}, DataFromMem[15:0]};  // Bit_Extender bit_extender_5
  assign bit_extender_6_out = {{16{DataFromMem[23]}}, DataFromMem[23:8]};  // Bit_Extender bit_extender_6
  assign bit_extender_7_out = {{16{DataFromMem[31]}}, DataFromMem[31:16]};  // Bit_Extender bit_extender_7
  Multiplexer #(.select(2), .width(32)) multiplexer_1 (
    .in0(bit_extender_1_out), .in1(bit_extender_2_out), .in2(bit_extender_3_out), .in3(bit_extender_4_out),
    .out(multiplexer_1_out), .sel(BOT_TWO_BITS));
  Multiplexer #(.select(2), .width(32)) multiplexer_2 (
    .in0(bit_extender_5_out), .in1(bit_extender_6_out), .in2(bit_extender_7_out), .out(multiplexer_2_out),
    .sel(BOT_TWO_BITS));  // open: in3
  Bit_Extender #(.in_width(32), .out_width(2)) bit_extender_8 (.in(MemAddress), .out(BOT_TWO_BITS));
  Multiplexer #(.select(3), .width(32)) multiplexer_3 (
    .in0(multiplexer_1_out), .in1(multiplexer_2_out), .in2(DataFromMem), .out(DataToReg),
    .sel(Instruction[14:12]));  // open: in3, in4, in5, in6, in7

  // Other names for the same wires on the sheet: Funct3[2:0] = Instruction[14:12]

  // Notes on the sheet:
  //   INPUTS to your circuit
  //   DON'T CHANGE THE LOCATIONS OF THE INPUTS AND OUTPUTS!
  //   OUTPUT from your circuit
endmodule
